// Logisim project Sumador.circ as structural Verilog: 1 circuit, main circuit main
module main (
  input  [3:0] A,
  input  [3:0] B,
  input  in_3,
  input  in_4,
  input  in_5,
  input  in_6,
  input  in_7,
  input  in_8,
  input  in_9,
  input  in_10,
  output [3:0] salida,
  output carry,
  output out_13,
  output out_14,
  output out_15,
  output out_16,
  output out_17
);

  wire and_1_out, and_2_out, and_3_out;

  Adder #(.width(4)) adder_1 (.a(A), .b(B), .out(salida), .cin(1'b0), .cout(carry));
  xor xor_1 (out_15, in_6, in_10);
  and and_1 (and_1_out, in_6, in_10);
  ExactlyOne xor_2 (.out(out_14), .in1(in_5), .in2(and_1_out), .in3(in_9));
  and and_2 (and_2_out, in_5, in_9);
  ExactlyOne xor_3 (.out(out_13), .in1(and_2_out), .in2(in_4), .in3(in_8));
  and and_3 (and_3_out, in_4, in_8);
  ExactlyOne xor_4 (.out(out_17), .in1(and_3_out), .in2(in_3), .in3(in_7));
  and and_4 (out_16, in_3, in_7);
  RAM ram_1 ();  // open: addr, data, sel, clk, ld, clr

  // Notes on the sheet:
  //   Sumador como tal
endmodule
